// Logisim project comp_2.circ as structural Verilog: 5 circuits, main circuit main
module main (
  input  [7:0] in_1,
  input  [4:0] Opcode__FIXME,
  input  PC_Control__FIXME,
  input  Reset_PC,
  input  Read_Write
);

  wire alu_1_branch_output, clock_1_out;
  wire [2:0] undriven_2, undriven_3, undriven_4;
  wire [7:0] adder_1_out, alu_1_arithmetic_output, counter_1_q, multiplexer_1_out, ram_2_data,
       register_file_1_read_data_1, register_file_1_read_data_2, undriven;
  wire [19:0] ram_1_data;

  Clock clock_1 (.out(clock_1_out));
  Multiplexer #(.width(8), .enable("false")) multiplexer_1 (
    .in0(in_1), .in1(undriven), .out(multiplexer_1_out), .sel(PC_Control__FIXME));
  Adder adder_1 (.a(multiplexer_1_out), .b(counter_1_q), .out(adder_1_out));  // open: cin, cout
  Counter counter_1 (.D(adder_1_out), .Q(counter_1_q), .clk(clock_1_out), .clr(Reset_PC));  // open: load, count, carry
  RAM #(.dataWidth(20)) ram_1 (.addr(counter_1_q), .data(ram_1_data), .clk(clock_1_out));  // open: sel, ld, clr
  Register_File register_file_1 (
    .Read_Address_1(undriven_2), .Read_Address_2(undriven_3), .Write_Address(undriven_4),
    .Write_Data(ram_2_data), .Read_Write(Read_Write), .Clock(clock_1_out),
    .Read_Data_1(register_file_1_read_data_1), .Read_Data_2(register_file_1_read_data_2));
  ALU alu_1 (
    .Input_1(register_file_1_read_data_1), .Input_2(register_file_1_read_data_2), .Opcode(Opcode__FIXME),
    .Branch_Output(alu_1_branch_output), .Arithmetic_Output(alu_1_arithmetic_output));
  RAM #(.bus("separate")) ram_2 (
    .addr(alu_1_arithmetic_output), .din(register_file_1_read_data_1), .data(ram_2_data), .clk(clock_1_out));  // open: str, sel, ld, clr

  // Notes on the sheet:
  //   Instruction Memory
  //   Splitter
  //   Register File
  //   ALU
  //   Data Memory
endmodule

module Register_File (
  input  [2:0] Read_Address_1,
  input  [2:0] Read_Address_2,
  input  [2:0] Write_Address,
  input  [7:0] Write_Data,
  input  Read_Write,
  input  Clock,
  output [7:0] Read_Data_1,
  output [7:0] Read_Data_2
);

  wire decoder_1_out1, decoder_1_out2, decoder_1_out3, decoder_1_out4, decoder_1_out5, decoder_1_out6,
       decoder_1_out7;
  wire [7:0] register_1_q, register_2_q, register_3_q, register_4_q, register_5_q, register_6_q,
       register_7_q, register_8_q;

  Decoder #(.select(3), .disabled(0)) decoder_1 (
    .out1(decoder_1_out1), .out2(decoder_1_out2), .out3(decoder_1_out3), .out4(decoder_1_out4),
    .out5(decoder_1_out5), .out6(decoder_1_out6), .out7(decoder_1_out7), .sel(Write_Address), .en(Read_Write));  // open: out0
  Register register_1 (.Q(register_1_q));  // open: D, en, clk, clr
  Register register_2 (.D(Write_Data), .en(decoder_1_out1), .Q(register_2_q), .clk(Clock));  // open: clr
  Register register_3 (.D(Write_Data), .en(decoder_1_out2), .Q(register_3_q), .clk(Clock));  // open: clr
  Register register_4 (.D(Write_Data), .en(decoder_1_out3), .Q(register_4_q), .clk(Clock));  // open: clr
  Register register_5 (.D(Write_Data), .en(decoder_1_out4), .Q(register_5_q), .clk(Clock));  // open: clr
  Register register_6 (.D(Write_Data), .en(decoder_1_out5), .Q(register_6_q), .clk(Clock));  // open: clr
  Register register_7 (.D(Write_Data), .en(decoder_1_out6), .Q(register_7_q), .clk(Clock));  // open: clr
  Register register_8 (.D(Write_Data), .en(decoder_1_out7), .Q(register_8_q), .clk(Clock));  // open: clr
  Multiplexer #(.select(3), .width(8), .enable("false")) multiplexer_1 (
    .in0(register_1_q), .in1(register_2_q), .in2(register_3_q), .in3(register_4_q), .in4(register_5_q),
    .in5(register_6_q), .in6(register_7_q), .in7(register_8_q), .out(Read_Data_1), .sel(Read_Address_1));
  Multiplexer #(.select(3), .width(8), .enable("false")) multiplexer_2 (
    .in0(register_1_q), .in1(register_2_q), .in2(register_3_q), .in3(register_4_q), .in4(register_5_q),
    .in5(register_6_q), .in6(register_7_q), .in7(register_8_q), .out(Read_Data_2), .sel(Read_Address_2));
endmodule

module test_register_file (
  input  [2:0] Read_Address_1,
  input  [2:0] Read_Address_2,
  input  [2:0] Write_Address,
  input  [7:0] Write_Data,
  input  Read_Write,
  output [7:0] Read_Data_1,
  output [7:0] Read_Data_2
);

  wire clock_1_out;

  Register_File register_file_1 (
    .Read_Address_1(Read_Address_1), .Read_Address_2(Read_Address_2), .Write_Address(Write_Address),
    .Write_Data(Write_Data), .Read_Write(Read_Write), .Clock(clock_1_out), .Read_Data_1(Read_Data_1),
    .Read_Data_2(Read_Data_2));
  Clock clock_1 (.out(clock_1_out));

  // Notes on the sheet:
  //   Register File
endmodule

module ALU (
  input  [4:0] Opcode,
  input  [7:0] Input_1,
  input  [7:0] Input_2,
  output Branch_Output,
  output [7:0] Arithmetic_Output
);

  wire [7:0] adder_1_out;

  Comparator comparator_1 (.a(Input_1), .b(Input_2));  // open: gt, eq, lt
  Adder adder_1 (.a(Input_1), .b(Input_2), .out(adder_1_out));  // open: cin, cout
  Multiplexer #(.select(5), .width(8), .enable("false")) multiplexer_1 (
    .in2(adder_1_out), .in3(adder_1_out), .out(Arithmetic_Output), .sel(Opcode));  // open: in0, in1, in4, in5, in6, in7, in8, in9, in10, in11, in12, in13, in14, in15, in16, in17, in18, in19, in20, in21, in22, in23, in24, in25, in26, in27, in28, in29, in30, in31

  // Notes on the sheet:
  //   TODO: Fill in the other instructions that use the ALU
endmodule

module test_alu (
  input  [4:0] Opcode,
  input  [7:0] Input_1,
  input  [7:0] Input_2,
  output Branch_Output,
  output [7:0] Arithmetic_Output
);

  ALU alu_1 (
    .Input_1(Input_1), .Input_2(Input_2), .Opcode(Opcode), .Branch_Output(Branch_Output),
    .Arithmetic_Output(Arithmetic_Output));

  // Notes on the sheet:
  //   TODO: After generating Branch Output, think about how to hook into PC
endmodule
