// Logisim project pipelining.circ as structural Verilog: 6 circuits, main circuit using_ripple_carry
module FA (
  input  A,
  input  B,
  input  Cin,
  output S,
  output Cout
);

  wire and_1_out, and_2_out, xor_1_out;

  xor xor_1 (xor_1_out, A, B);
  xor xor_2 (S, xor_1_out, Cin);
  and and_1 (and_1_out, xor_1_out, Cin);
  and and_2 (and_2_out, A, B);
  or or_1 (Cout, and_1_out, and_2_out);
endmodule

module HA (
  input  A,
  input  B,
  output S,
  output Cout
);

  xor xor_1 (S, A, B);
  and and_1 (Cout, A, B);
endmodule

module ripple_carry (
  input  [3:0] A,
  input  [3:0] B,
  output [3:0] C
);

  wire fa_1_cout, fa_2_cout, ha_1_cout;

  HA ha_1 (.A(A[0]), .B(B[0]), .S(C[0]), .Cout(ha_1_cout));
  FA fa_1 (.A(A[1]), .B(B[1]), .Cin(ha_1_cout), .S(C[1]), .Cout(fa_1_cout));
  FA fa_2 (.A(A[2]), .B(B[2]), .Cin(fa_1_cout), .S(C[2]), .Cout(fa_2_cout));
  FA fa_3 (.A(A[3]), .B(B[3]), .Cin(fa_2_cout), .S(C[3]));  // open: Cout

  // Notes on the sheet:
  //   HA
  //   FA
  //   FA
  //   FA
endmodule

module using_ripple_carry (
);

  wire clock_1_out, clock_2_out, clock_3_out;
  wire [3:0] buf_ripple_carry_1_c, pipe_ripple_carry_1_c, register_1_q, register_2_q, register_3_q,
       register_4_q, register_5_q, register_6_q, ripple_carry_1_c;

  Register #(.width(4)) register_1 (.Q(register_1_q), .clk(clock_1_out));  // open: D, en, clr
  Register #(.width(4)) register_2 (.Q(register_2_q), .clk(clock_1_out));  // open: D, en, clr
  Clock clock_1 (.out(clock_1_out));
  Register #(.width(4)) register_3 (.Q(register_3_q), .clk(clock_2_out));  // open: D, en, clr
  Register #(.width(4)) register_4 (.Q(register_4_q), .clk(clock_2_out));  // open: D, en, clr
  Clock clock_2 (.out(clock_2_out));
  Register #(.width(4)) register_5 (.Q(register_5_q), .clk(clock_3_out));  // open: D, en, clr
  Register #(.width(4)) register_6 (.Q(register_6_q), .clk(clock_3_out));  // open: D, en, clr
  Clock clock_3 (.out(clock_3_out));
  ripple_carry ripple_carry_1 (.A(register_1_q), .B(register_2_q), .C(ripple_carry_1_c));
  buf_ripple_carry buf_ripple_carry_1 (
    .A(register_3_q), .B(register_4_q), .Clock(clock_2_out), .C(buf_ripple_carry_1_c));
  pipe_ripple_carry pipe_ripple_carry_1 (
    .A(register_5_q), .B(register_6_q), .C(pipe_ripple_carry_1_c), .Clock(clock_3_out));
  Register #(.width(4)) register_7 (.D(ripple_carry_1_c), .clk(clock_1_out));  // open: en, Q, clr
  Register #(.width(4)) register_8 (.D(buf_ripple_carry_1_c), .clk(clock_2_out));  // open: en, Q, clr
  Register #(.width(4)) register_9 (.D(pipe_ripple_carry_1_c), .clk(clock_3_out));  // open: en, Q, clr

  // Notes on the sheet:
  //   4-bit
  //   Ripple Carry
  //   Buffered
  //   4-bit
  //   Ripple Carry
  //   Pipelined
  //   4-bit
  //   Ripple Carry
endmodule

module pipe_ripple_carry (
  input  [3:0] A,
  input  [3:0] B,
  input  Clock,
  output [3:0] C
);

  wire fa_1_cout, fa_1_s, fa_2_cout, fa_2_s, ha_1_cout, ha_1_s, register_1_q, register_2_q, register_3_q,
       shift_register_1_out, shift_register_2_out, shift_register_3_out, shift_register_4_out,
       shift_register_5_out, shift_register_6_out;

  Shift_Register #(.length(3)) shift_register_1 (
    .in(A[3]), .clk(Clock), .out(shift_register_1_out));  // open: shift, load, clr, d0, q0, d1, q1, d2, q2
  Shift_Register #(.length(2)) shift_register_2 (
    .in(A[2]), .clk(Clock), .out(shift_register_2_out));  // open: shift, load, clr, d0, q0, d1, q1
  Shift_Register #(.length(1)) shift_register_3 (
    .in(A[1]), .clk(Clock), .out(shift_register_3_out));  // open: shift, load, clr, d0, q0
  Shift_Register #(.length(3)) shift_register_4 (
    .in(B[3]), .clk(Clock), .out(shift_register_4_out));  // open: shift, load, clr, d0, q0, d1, q1, d2, q2
  Shift_Register #(.length(2)) shift_register_5 (
    .in(B[2]), .clk(Clock), .out(shift_register_5_out));  // open: shift, load, clr, d0, q0, d1, q1
  Shift_Register #(.length(1)) shift_register_6 (
    .in(B[1]), .clk(Clock), .out(shift_register_6_out));  // open: shift, load, clr, d0, q0
  HA ha_1 (.A(A[0]), .B(B[0]), .S(ha_1_s), .Cout(ha_1_cout));
  Register #(.width(1)) register_1 (.D(ha_1_cout), .Q(register_1_q), .clk(Clock));  // open: en, clr
  FA fa_1 (.A(shift_register_3_out), .B(shift_register_6_out), .Cin(register_1_q), .S(fa_1_s), .Cout(fa_1_cout));
  Register #(.width(1)) register_2 (.D(fa_1_cout), .Q(register_2_q), .clk(Clock));  // open: en, clr
  FA fa_2 (.A(shift_register_2_out), .B(shift_register_5_out), .Cin(register_2_q), .S(fa_2_s), .Cout(fa_2_cout));
  Register #(.width(1)) register_3 (.D(fa_2_cout), .Q(register_3_q), .clk(Clock));  // open: en, clr
  FA fa_3 (.A(shift_register_1_out), .B(shift_register_4_out), .Cin(register_3_q), .S(C[3]));  // open: Cout
  Shift_Register #(.length(1)) shift_register_7 (
    .in(fa_2_s), .clk(Clock), .out(C[2]));  // open: shift, load, clr, d0, q0
  Shift_Register #(.length(2)) shift_register_8 (
    .in(fa_1_s), .clk(Clock), .out(C[1]));  // open: shift, load, clr, d0, q0, d1, q1
  Shift_Register #(.length(3)) shift_register_9 (
    .in(ha_1_s), .clk(Clock), .out(C[0]));  // open: shift, load, clr, d0, q0, d1, q1, d2, q2

  // Notes on the sheet:
  //   Input
  //   Shift Registers
  //   HA
  //   Register
  //   Register
  //   FA
  //   FA
  //   Register
  //   FA
  //   Output
  //   Shift Registers
endmodule

module buf_ripple_carry (
  input  [3:0] A,
  input  [3:0] B,
  input  Clock,
  output [3:0] C
);

  wire counter_1_carry, fa_1_cout, fa_2_cout, ha_1_cout, register_1_q, register_2_q, register_3_q;
  wire [3:0] ha_1_s;

  HA ha_1 (.A(A[0]), .B(B[0]), .S(ha_1_s[0]), .Cout(ha_1_cout));
  Register #(.width(1)) register_1 (.D(ha_1_cout), .Q(register_1_q), .clk(Clock));  // open: en, clr
  FA fa_1 (.A(A[1]), .B(B[1]), .Cin(register_1_q), .S(ha_1_s[1]), .Cout(fa_1_cout));
  Register #(.width(1)) register_2 (.D(fa_1_cout), .Q(register_2_q), .clk(Clock));  // open: en, clr
  FA fa_2 (.A(A[2]), .B(B[2]), .Cin(register_2_q), .S(ha_1_s[2]), .Cout(fa_2_cout));
  Register #(.width(1)) register_3 (.D(fa_2_cout), .Q(register_3_q), .clk(Clock));  // open: en, clr
  FA fa_3 (.A(A[3]), .B(B[3]), .Cin(register_3_q), .S(ha_1_s[3]));  // open: Cout
  Counter #(.width(2), .max('h3)) counter_1 (.carry(counter_1_carry), .clk(Clock));  // open: load, D, count, Q, clr
  assign C = counter_1_carry ? ha_1_s : 4'bz;  // Controlled_Buffer controlled_buffer_1

  // Notes on the sheet:
  //   HA
  //   Register
  //   FA
  //   Register
  //   FA
  //   Register
  //   FA
  //   Counter
endmodule
